# Fritzing sketch oda denemesi (saved by Fritzing 0.9.3b)
breadboards: 1

parts:
  Parça1 = Arduino Uno (Rev3)
  BT1 = Bluetooth HC-06d [package=THT]
  LED1 = RGB LED (com. anode, rbg) [package="5 mm [THT]"]
  R1 = Resistor [tolerance=±5% resistance=220 package="2512 [SMD]"]  # not connected
  R2 = Resistor [tolerance=±5% resistance=220 package="2512 [SMD]"]
  R3 = Resistor [tolerance=±5% resistance=220 package="2512 [SMD]"]

nets:
  N1: Parça1.D0/RX, BT1.TXD
  N2: Parça1.D1/TX, BT1.RXD
  5V: Parça1.5V, BT1.VCC
  GND: Parça1.GND, BT1.GND
  N3: LED1.blue_cathode, R2.Pin_0
  N4: LED1.green_cathode, R3.Pin_0

custom parts:
  Bluetooth HC-06d: Bluetooth HC-06 - face down, pins down 16.5mm x 37.5mm PCB
